# Fritzing sketch truc (saved by Fritzing 0.9.2b)
circuit board: 1.90524cm x 4.41223cm
breadboards: 1

parts:
  RGB_Led = RGB LED (com. cathode, rbg) [package="5 mm [THT]"]
  LDR = Photocell (LDR) [package=THT]
  R1_(220) = Resistor [tolerance=±5% resistance=220 package=THT]
  R2_(10k) = Resistor [tolerance=±5% resistance=10k package=THT]
  Buzzer = Piezo Speaker
  Arduino_Nano = Arduino Nano (Rev3.0)

nets:
  N1: RGB_Led.red_anode, Arduino_Nano.D3
  N2: RGB_Led.common_cathode, R1_(220).Pin_0
  N3: RGB_Led.blue_anode, Arduino_Nano.D4
  N4: RGB_Led.green_anode, Arduino_Nano.D5
  N5: LDR.pin_0, Arduino_Nano.5V
  N6: LDR.pin_1, R2_(10k).Pin_0, Arduino_Nano.A0
  N7: R1_(220).Pin_1, R2_(10k).Pin_1, Buzzer.pin1, Arduino_Nano.GND
  N8: Buzzer.pin2, Arduino_Nano.D11/MOSI

notes:
  lateliersadapte.org
  Nuance proto#1
  Prototype v1
  (27/03/16)
